// Logisim project COA_FINAL_LOGISIM.circ as structural Verilog
module project_ao (
  input  [15:0] A,
  input  [3:0] AUSel,
  input  [15:0] B,
  output [15:0] AUResult
);

  wire [15:0] adder_1_out, and_1_out, divider_1_out, divider_2_rem, multiplier_1_out, negator_1_out,
       negator_2_out, or_1_out, shifter_1_out, shifter_2_out, shifter_3_out, shifter_4_out, subtractor_1_out,
       xor_1_out;

  Adder #(.width(16)) adder_1 (.a(A), .b(B), .out(adder_1_out));  // open: cin, cout
  assign and_1_out = A & B;  // AND_Gate and_1, 16 bits wide
  assign or_1_out = A | B;  // OR_Gate or_1, 16 bits wide
  assign xor_1_out = A ^ B;  // XOR_Gate xor_1, 16 bits wide
  Divider #(.width(16)) divider_1 (.a(A), .b(B), .out(divider_1_out));  // open: upper, rem
  Divider #(.width(16)) divider_2 (.a(A), .b(B), .rem(divider_2_rem));  // open: out, upper
  Multiplier #(.width(16)) multiplier_1 (.a(A), .b(B), .out(multiplier_1_out));  // open: cin, cout
  Subtractor #(.width(16)) subtractor_1 (.a(A), .b(B), .out(subtractor_1_out));  // open: bin, bout
  Shifter #(.width(16)) shifter_1 (.in(A), .\dist (4'b0010), .out(shifter_1_out));
  Shifter #(.width(16)) shifter_2 (.in(B), .\dist (4'b0010), .out(shifter_2_out));
  Shifter #(.shift("lr"), .width(16)) shifter_3 (.in(A), .\dist (4'b0010), .out(shifter_3_out));
  Shifter #(.shift("lr"), .width(16)) shifter_4 (.in(B), .\dist (4'b0010), .out(shifter_4_out));
  Negator #(.width(16)) negator_1 (.in(A), .out(negator_1_out));
  Negator #(.width(16)) negator_2 (.in(B), .out(negator_2_out));
  Multiplexer #(.select(4), .width(16)) multiplexer_1 (
    .in0(adder_1_out), .in1(and_1_out), .in2(or_1_out), .in3(xor_1_out), .in4(divider_1_out),
    .in5(divider_2_rem), .in6(multiplier_1_out), .in7(subtractor_1_out), .in8(shifter_1_out),
    .in9(shifter_2_out), .in10(shifter_3_out), .in11(shifter_4_out), .in12(negator_1_out),
    .in13(negator_2_out), .out(AUResult), .sel(AUSel));  // open: in14, in15
endmodule

module project_ro (
  input  [15:0] A,
  input  [15:0] B,
  input  [2:0] RUSel,
  output result
);

  wire comparator_1_eq, comparator_1_gt, comparator_1_lt, not_1_out, or_1_out, or_2_out;

  Comparator #(.mode("unsigned"), .width(16)) comparator_1 (
    .a(A), .b(B), .gt(comparator_1_gt), .eq(comparator_1_eq), .lt(comparator_1_lt));
  or or_1 (or_1_out, comparator_1_gt, comparator_1_eq);
  or or_2 (or_2_out, comparator_1_eq, comparator_1_lt);
  not not_1 (not_1_out, comparator_1_eq);
  Multiplexer #(.select(3)) multiplexer_1 (
    .in0(or_1_out), .in1(comparator_1_gt), .in2(comparator_1_eq), .in3(comparator_1_lt), .in4(or_2_out),
    .in5(not_1_out), .out(result), .sel(RUSel));  // open: in6, in7

  // Notes on the sheet:
  //   Logic Unit (LU)
  //   >=
  //   >
  //   =
  //   <
  //   <=
  //   !=
endmodule

module project_alu (
  input  [15:0] A,
  input  [15:0] B,
  input  [3:0] au_sel,
  input  [2:0] ru_sel,
  input  OE,
  output [15:0] AUDout,
  output [15:0] AUResult,
  output RUResult
);

  project_ao project_ao_1 (.A(A), .AUSel(au_sel), .B(B), .AUResult(AUResult));
  project_ro project_ro_1 (.A(A), .B(B), .RUSel(ru_sel), .result(RUResult));
  assign AUDout = OE ? AUResult : 16'bz;  // Controlled_Buffer controlled_buffer_1
endmodule

module reg16bit (
  input  [15:0] Din,
  input  we,
  input  clk,
  input  reset,
  input  oe,
  output [15:0] SD,
  output [15:0] Dout,
  output [7:0] out_8,
  output [7:0] out_9
);

  Register #(.width(16)) register_1 (.D(Din), .en(we), .clk(clk), .Q(SD), .clr(reset));
  assign Dout = oe ? SD : 16'bz;  // Controlled_Buffer controlled_buffer_1
  BitSelector #(.group(8), .width(16)) bitselector_1 (.in(Dout), .out(out_8), .sel(1'b0));
  BitSelector #(.group(8), .width(16)) bitselector_2 (.in(Dout), .out(out_9), .sel(1'b1));
endmodule

module datapath (
  input  [15:0] test_data,
  input  we_mar,
  input  oe_test,
  input  oe_mar,
  input  intrnl_oe_mar,
  input  we_mbr,
  input  oe_mbr,
  input  we_ir,
  input  reset_ir,
  input  oe_ir,
  input  we_rega,
  input  reset_rega,
  input  [3:0] au_sel,
  input  we_or,
  input  [2:0] ru_sel,
  input  oe_alu,
  input  oe_or,
  input  we_regb,
  input  reset_regb,
  output [7:0] content_mar,
  output [15:0] content_ir,
  output [15:0] out_22,
  output [15:0] sd_rega,
  output [15:0] out_24,
  output [15:0] sd_or,
  output out_26,
  output [15:0] sd_regb
);

  wire clock_1_out;
  wire [7:0] bitselector_1_out, reg8bit_1_dout;
  wire [15:0] project_alu_1_audout, reg16bit_1_dout, reg16bit_2_dout;

  Clock clock_1 (.out(clock_1_out));
  LED D15 (.in(project_alu_1_audout[15]));
  BitSelector #(.group(8), .width(16)) bitselector_1 (.in(reg16bit_1_dout), .out(bitselector_1_out), .sel(1'b0));
  reg16bit reg16bit_1 (
    .Din(project_alu_1_audout), .we(we_ir), .clk(clock_1_out), .reset(reset_ir), .oe(oe_ir), .SD(content_ir),
    .Dout(reg16bit_1_dout));  // open: out_8, out_9
  reg16bit reg16bit_2 (
    .Din(project_alu_1_audout), .we(we_rega), .clk(clock_1_out), .reset(reset_rega), .SD(sd_rega),
    .Dout(reg16bit_2_dout));  // open: oe, out_8, out_9
  project_alu project_alu_1 (
    .A(sd_rega), .B(sd_regb), .au_sel(au_sel), .ru_sel(ru_sel), .OE(oe_alu), .AUDout(project_alu_1_audout),
    .AUResult(out_24), .RUResult(out_26));
  reg16bit reg16bit_3 (
    .Din(project_alu_1_audout), .we(we_regb), .clk(clock_1_out), .reset(reset_regb), .SD(sd_regb));  // open: oe, Dout, out_8, out_9
  LED D14 (.in(project_alu_1_audout[14]));
  LED D13 (.in(project_alu_1_audout[13]));
  LED D12 (.in(project_alu_1_audout[12]));
  LED D11 (.in(project_alu_1_audout[11]));
  LED D10 (.in(project_alu_1_audout[10]));
  assign project_alu_1_audout = oe_test ? test_data : 16'bz;  // Controlled_Buffer controlled_buffer_1
  LED D9 (.in(project_alu_1_audout[9]));
  LED D8 (.in(project_alu_1_audout[8]));
  LED D7 (.in(project_alu_1_audout[7]));
  LED D6 (.in(project_alu_1_audout[6]));
  LED D5 (.in(project_alu_1_audout[5]));
  LED D4 (.in(project_alu_1_audout[4]));
  LED D3 (.in(project_alu_1_audout[3]));
  assign project_alu_1_audout = intrnl_oe_mar ? out_22 : 16'bz;  // Controlled_Buffer controlled_buffer_2
  LED D2 (.in(project_alu_1_audout[2]));
  LED D1 (.in(project_alu_1_audout[1]));
  LED D0 (.in(project_alu_1_audout[0]));
  reg8bit reg8bit_1 (
    .Din(bitselector_1_out), .we(we_mar), .clk(clock_1_out), .oe(oe_mar), .SD(content_mar),
    .Dout(reg8bit_1_dout));  // open: reset
  reg16bit reg16bit_4 (
    .Din(project_alu_1_audout), .we(we_mbr), .clk(clock_1_out), .oe(oe_mbr), .SD(out_22),
    .Dout(project_alu_1_audout));  // open: reset, out_8, out_9
  reg16bit reg16bit_5 (
    .Din(project_alu_1_audout), .we(we_or), .clk(clock_1_out), .oe(oe_or), .SD(sd_or),
    .Dout(project_alu_1_audout));  // open: reset, out_8, out_9
  LED led_1 (.in(project_alu_1_audout[15]));
  LED led_2 (.in(project_alu_1_audout[14]));
  LED led_3 (.in(project_alu_1_audout[13]));
  LED led_4 (.in(project_alu_1_audout[12]));
  LED led_5 (.in(project_alu_1_audout[11]));
  LED led_6 (.in(project_alu_1_audout[10]));
  LED led_7 (.in(project_alu_1_audout[9]));
  LED led_8 (.in(project_alu_1_audout[8]));
  LED led_9 (.in(project_alu_1_audout[7]));
  LED led_10 (.in(project_alu_1_audout[6]));
  LED led_11 (.in(project_alu_1_audout[5]));
  LED led_12 (.in(project_alu_1_audout[4]));
  LED led_13 (.in(project_alu_1_audout[3]));
  LED led_14 (.in(project_alu_1_audout[2]));
  LED led_15 (.in(project_alu_1_audout[1]));
  LED led_16 (.in(project_alu_1_audout[0]));

  // Notes on the sheet:
  //   Instruction Register
  //   registerA
  //   ALU
  //   registerB
  //   Internal Address Bus (8-bits)
  //   MAR
  //   MBR
  //   Output Register
endmodule

module reg8bit (
  input  [7:0] Din,
  input  we,
  input  clk,
  input  reset,
  input  oe,
  output [7:0] SD,
  output [7:0] Dout
);

  Register register_1 (.D(Din), .en(we), .clk(clk), .Q(SD), .clr(reset));
  assign Dout = oe ? SD : 8'bz;  // Controlled_Buffer controlled_buffer_1
endmodule
